// Logisim project adder_subtractor_8bit.circ as structural Verilog: 3 circuits, main circuit main
module main (
  input  switch,
  input  [7:0] in_2,
  input  [7:0] in_3,
  output [7:0] out_4,
  output [7:0] Result
);

  wire adder_subtractor_1bit_2_cout, adder_subtractor_1bit_3_cout, adder_subtractor_1bit_4_cout,
       adder_subtractor_1bit_5_cout, adder_subtractor_1bit_6_cout, adder_subtractor_1bit_7_cout,
       adder_subtractor_1bit_8_cout;

  Adder_Subtractor_1bit adder_subtractor_1bit_1 (
    .A(in_2[7]), .B(in_3[7]), .sub(switch), .Cin(adder_subtractor_1bit_2_cout), .Sum(out_4[7]));  // open: Cout
  Adder_Subtractor_1bit adder_subtractor_1bit_2 (
    .A(in_2[6]), .B(in_3[6]), .sub(switch), .Cin(adder_subtractor_1bit_3_cout), .Sum(out_4[6]),
    .Cout(adder_subtractor_1bit_2_cout));
  Adder_Subtractor_1bit adder_subtractor_1bit_3 (
    .A(in_2[5]), .B(in_3[5]), .sub(switch), .Cin(adder_subtractor_1bit_4_cout), .Sum(out_4[5]),
    .Cout(adder_subtractor_1bit_3_cout));
  Adder_Subtractor_1bit adder_subtractor_1bit_4 (
    .A(in_2[4]), .B(in_3[4]), .sub(switch), .Cin(adder_subtractor_1bit_5_cout), .Sum(out_4[4]),
    .Cout(adder_subtractor_1bit_4_cout));
  Adder_Subtractor_1bit adder_subtractor_1bit_5 (
    .A(in_2[3]), .B(in_3[3]), .sub(switch), .Cin(adder_subtractor_1bit_6_cout), .Sum(out_4[3]),
    .Cout(adder_subtractor_1bit_5_cout));
  Adder_Subtractor_1bit adder_subtractor_1bit_6 (
    .A(in_2[2]), .B(in_3[2]), .sub(switch), .Cin(adder_subtractor_1bit_7_cout), .Sum(out_4[2]),
    .Cout(adder_subtractor_1bit_6_cout));
  Adder_Subtractor_1bit adder_subtractor_1bit_7 (
    .A(in_2[1]), .B(in_3[1]), .sub(switch), .Cin(adder_subtractor_1bit_8_cout), .Sum(out_4[1]),
    .Cout(adder_subtractor_1bit_7_cout));
  Adder_Subtractor_1bit adder_subtractor_1bit_8 (
    .A(in_2[0]), .B(in_3[0]), .sub(switch), .Cin(switch), .Sum(out_4[0]), .Cout(adder_subtractor_1bit_8_cout));

  assign Result = out_4;

  // Other names for the same wires on the sheet: A0 = in_2[0]; A1 = in_2[1]; A2 = in_2[2]; A3 = in_2[3]; A4 = in_2[4];
  //   A5 = in_2[5]; A6 = in_2[6]; A7 = in_2[7]; B0 = in_3[0]; B1 = in_3[1]; B2 = in_3[2]; B3 = in_3[3]; B4 = in_3[4];
  //   B5 = in_3[5]; B6 = in_3[6]; B7 = in_3[7]; S0 = out_4[0]; S1 = out_4[1]; S2 = out_4[2]; S3 = out_4[3];
  //   S4 = out_4[4]; S5 = out_4[5]; S6 = out_4[6]; S7 = out_4[7]
endmodule

// Sum
module Full_Adder_1bit (
  input  A,
  input  B,
  input  Cin,
  output Sum,
  output Cout
);

  wire and_1_out, and_2_out, xor_1_out;

  and and_1 (and_1_out, B, A);
  xor xor_1 (xor_1_out, A, B);
  xor xor_2 (Sum, xor_1_out, Cin);
  and and_2 (and_2_out, xor_1_out, Cin);
  or or_1 (Cout, and_2_out, and_1_out);
endmodule

// A
module Adder_Subtractor_1bit (
  input  A,
  input  B,
  input  sub,
  input  Cin,
  output Sum,
  output Cout
);

  wire xor_1_out;

  xor xor_1 (xor_1_out, B, sub);
  Full_Adder_1bit full_adder_1bit_1 (.A(A), .B(xor_1_out), .Cin(Cin), .Sum(Sum), .Cout(Cout));
endmodule
